# Fritzing sketch circuit (saved by Fritzing 0.9.3b)
circuit board: 6.27995cm x 5.49044cm

parts:
  Pro_Mini = Arduino Pro Mini V2 (5V)
  RCWL-0516 = RCWL-0516 Microwave Radar Motion Sensor Module
  MAX9814 = Adafruit MAX9814 Electret Microphone Amplifier [part_number="Adafruit #1713"]
  Buzz = Piezo Speaker
  NeoPixels = Dagu DGServo 9g header (male) [package=THT]
  -_+ = female pin header, 2 pins [form="♀ (female)"]
  SERIAL = female pin header, 6 pins [form="♀ (female)"]
  J1 = Piezo Speaker
  R2 = Resistor [tolerance=±5% resistance=220 package=THT]
  R1 = Resistor [tolerance=±5% resistance=220 package=THT]
  TOUCH = female pin header, 3 pins [form="♀ (female)"]
  GESTURE = female pin header, 5 pins [form="♀ (female)"]

nets:
  N1: Pro_Mini.DTR, SERIAL.pin6
  N2: Pro_Mini.TXO, SERIAL.pin5
  N3: Pro_Mini.RXI, SERIAL.pin4
  VCC: Pro_Mini.VCC, RCWL-0516.VIN, MAX9814.VDD, NeoPixels.Vcc, -_+.pin1, SERIAL.pin3, TOUCH.pin1, GESTURE.pin5
  GND: Pro_Mini.GND, RCWL-0516.GND, MAX9814.GND, Buzz.pin1, NeoPixels.gnd, -_+.pin2, SERIAL.pin2, J1.pin1, TOUCH.pin3, GESTURE.pin4
  N4: Pro_Mini.A4, GESTURE.pin2
  N5: Pro_Mini.A5, GESTURE.pin3
  N6: Pro_Mini.A0, MAX9814.OUTPUT
  N7: Pro_Mini.MOSI, R2.Pin_0
  N8: Pro_Mini.D10, R1.Pin_0
  N9: Pro_Mini.D3, TOUCH.pin2
  N10: Pro_Mini.D2, RCWL-0516.OUT
  N11: Buzz.pin2, J1.pin2, R2.Pin_1
  N12: NeoPixels.pulse, R1.Pin_1

custom parts:
  Arduino Pro Mini V2 (5V): Arduino Pro Mini V2 There are several different layouts for this board out there. This one is modeled after the Sparkfun 11113 board but a few of the pins have been moved around.
  RCWL-0516 Microwave Radar Motion Sensor Module: The RCWL-0516 is a microwave radar motion sensor module. Input voltage is 4V to 28V. The 3V3 pin is a power output.
  Adafruit MAX9814 Electret Microphone Amplifier: Add an ear to your project with this well-designed electret microphone amplifier with AGC. This fully assembled and tested board comes with a 20-20KHz electret microphone soldered on. For the amplification, we use the Maxim MAX9814, a specialty chip that is designed for amplifying electret microphones in situations where the loudness of the audio isn't predictable. This fancy microphone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
